# Fritzing sketch ckt diagram (saved by Fritzing 0.9.3b)

parts:
  Raspberry_Pi_1 = Raspberry Pi 3 [part_number=RPI-3-V1.2]
  CAMERA1 = TTL Serial JPEG Camera  # not connected
  M1 = BTS7960
  M2 = BTS7960
  Water_Level_Sensor1 = Water Level Sensor
  U1 = Mini-360 DC-DC Buck converter [package=THT]
  BAT1 = 12 battery [package=battery]

nets:
  N1: Raspberry_Pi_1.GPIO25, Water_Level_Sensor1.SIG
  GND: Raspberry_Pi_1.GND, Raspberry_Pi_1.GPIO23, M1.pin1, M1.pin2, M1.pin8, M2.pin3, M2.pin4, M2.pin8, Water_Level_Sensor1.GND
  N2: Raspberry_Pi_1.GPIO24, M2.pin1, M2.pin2
  N3: Raspberry_Pi_1.GPIO18, M1.pin3
  N4: Raspberry_Pi_1.GPIO15, M1.pin4
  5V: Raspberry_Pi_1.5V, M1.pin7, M2.pin7, Water_Level_Sensor1.VCC
  N5: M1.pin9, M2.pin9, U1.IN+, BAT1.+
  N6: M1.pin10, M2.pin10, U1.IN-, BAT1.-

custom parts:
  TTL Serial JPEG Camera: TTL Serial JPEG Camera with NTSC Out
  BTS7960: BTS7960 43A Peak Power H-Bridge PWM Motor Driver
  Water Level Sensor: A water level sensor. This sensor operates at 3V to 5V. The Sig (signal) pin outputs an analogue signal that is in proportion to the amount of water in contact with the sensor.
  Mini-360 DC-DC Buck converter: Mini-360 DC-DC Buck converter. Tiny buck step down voltage converter, input voltage 4.75 to 23V output 1 to 17V adjustable. Available from ebay and the like.
  12 battery: 12V lead acid type battery, like the Husqvarna YTH2448 12V 35AH battery. This is the mini version 1/4 the size of the actual battery to be closer to typical breadboard parts (around 2in wide rathher than 7in). The pads in pcb are sized to accomidate up to 14ga wire (as these batterys will deliver high currents.)
